# Fritzing sketch wiring_ProMini (saved by Fritzing 0.9.3b)

parts:
  Bauteil3 = Arduino Pro Mini (5V)
  R1 = Resistor [tolerance=±5% resistance=330 package="2010 [SMD]"]
  Config-Taster = Momentary Switch [package=ksa_sealed_tac_switch]
  U1 = CC1101 [part_number=CC1101]
  Bauteil4 = ws2812b [package="smd 2812b"]
  Bauteil5 = ws2812b [package="smd 2812b"]
  S4 = Momentary Switch [package=ksa_sealed_tac_switch]
  S5 = Momentary Switch [package=ksa_sealed_tac_switch]
  S6 = Momentary Switch [package=ksa_sealed_tac_switch]
  S7 = Momentary Switch [package=ksa_sealed_tac_switch]
  S8 = Momentary Switch [package=ksa_sealed_tac_switch]
  S9 = Momentary Switch [package=ksa_sealed_tac_switch]
  R2 = Resistor [tolerance=±5% resistance=330 package="2010 [SMD]"]
  Duo-LED = DUO LED RG [package="5 mm [THT]"]

nets:
  N1: Bauteil3.A4, S5.2
  N2: Bauteil3.A5, S4.2
  VDD: Bauteil3.RAW, Bauteil4.VDD, Bauteil5.VDD
  VSS: Bauteil3.GND, Config-Taster.3, U1.2, Bauteil4.VSS, Bauteil5.VSS, S4.3, S5.3, Duo-LED.common_cathode
  N3: Bauteil3.VCC, U1.1
  N4: Bauteil3.A3, S6.2
  N5: Bauteil3.A2, S9.2
  N6: Bauteil3.A1, S7.2
  N7: Bauteil3.A0, S8.2
  N8: Bauteil3.SCK, U1.4
  N9: Bauteil3.MISO, U1.5
  N10: Bauteil3.MOSI, U1.3
  N11: Bauteil3.D10, U1.8
  N12: Bauteil3.D9, Bauteil4.DIN
  N13: Bauteil3.D8, Config-Taster.1
  N14: Bauteil3.D5, R2.Pin_1
  N15: Bauteil3.D4, R1.Pin_1
  N16: Bauteil3.D2, U1.7
  N17: R1.Pin_0, Duo-LED.green_anode
  N18: Bauteil4.DOUT, Bauteil5.DIN
  N19: R2.Pin_0, Duo-LED.red_anode

notes:
  +5V
  LED 1
  ...
  LED 6
  Taster 6 - 1
